# Fritzing sketch ShemaElectrique (saved by Fritzing 0.9.2b)
breadboards: 1

parts:
  Part2 = Arduino Mega 2560 (Rev3)
  U5 = SPM0204UD5 [package=spm0204ud5]
  Part3 = Arduino Uno (Rev3)
  NEOPIXEL1 = Neopixel Strip -- White (60/m)
  NEOPIXEL2 = Neopixel Strip -- White (60/m)
  NEOPIXEL3 = Neopixel Strip -- White (60/m)
  Power_plug1 = Power plug
  U6 = SPM0204UD5 [package=spm0204ud5]

nets:
  GND: Part2.GND, U5.GND, Part3.GND, NEOPIXEL1.GND, NEOPIXEL2.GND, NEOPIXEL3.GND, Power_plug1.GND, U6.GND
  N1: Part2.D11_PWM, U5.OUT
  N2: Part2.D10_PWM, U5.GND#
  N3: Part2.D9_PWM, U6.OUT
  N4: Part2.D8_PWM, U6.GND#
  5V: Part2.5V, U5.VS, NEOPIXEL1.+5V, NEOPIXEL2.+5V, NEOPIXEL3.+5V, Power_plug1.VCC, U6.VS
  N5: Part3.D8, NEOPIXEL3.DI
  N6: Part3.D4, NEOPIXEL1.DI
  N7: Part3.D6_PWM, NEOPIXEL2.DI

notes:
  Jeremy Ferland
  Charles-Olivier Belanger

custom parts:
  Neopixel Strip -- White (60/m): Neopixel Strip, White, 60 pixels per meter.
